# Fritzing sketch AAA-Tester (saved by Fritzing 0.9.10b)
breadboards: 2

parts:
  LCD1 = LCD screen  # not connected
  J1 = Screw terminal - 2 pins [package=THT]
  J2 = Screw terminal - 2 pins [package=THT]
  J3 = Screw terminal - 2 pins [package=THT]
  J4 = Screw terminal - 2 pins [package=THT]
  J5 = Screw terminal - 2 pins [package=THT]
  J6 = Screw terminal - 2 pins [package=THT]
  R1 = Resistor [tolerance=±5% power=0.25 resistance=10k package=THT]
  S1 = Pushbutton [package="[THT]"]
  S2 = Pushbutton [package="[THT]"]
  U1 = Voltage Regulator - 5V [package="TO220 [THT]"]
  Bauteil2 = Adafruit Datalogger Shield v1 [part_number="Adafruit #1141"]
  LED1 = LED - 5mm [color="Yellow (595nm)" current=0.030 package="5 mm [THT]"]
  LCM1 = LCM1602
  C1 = Electrolytic Capacitor [capacitance=033µF voltage=35V package="100 mil [THT, electrolytic]"]
  J8 = Screw terminal - 2 pins [package=THT]
  C2 = Electrolytic Capacitor [capacitance=0.1µF voltage=35V package="100 mil [THT, electrolytic]"]
  R2 = Resistor [tolerance=±5% power=0.25 resistance=10k package=THT]
  S3 = Pushbutton [package="[THT]"]
  R3 = Resistor [tolerance=±5% power=0.25 resistance=10k package=THT]
  J7 = Basic Servo
  R4 = Resistor [tolerance=±5% power=0.25 resistance=10k package=THT]
  R5 = Resistor [tolerance=±5% power=0.25 resistance=100 package=THT]
  R6 = Resistor [tolerance=±5% power=0.25 resistance=220 package=THT]
  SM1 = 28BYJ-48 Stepper Motor [part_number=28BYJ-48]
  Driver1 = 28BYJ-48 Driver Module [part_number=ULN2003 package=THT]
  Bauteil3 = Arduino Uno (Rev3)  # not connected
  Q2 = Basic FET N-Channel [package="TO220 [THT]"]
  R7 = Resistor [tolerance=±5% power=0.25 resistance=10k package=THT]
  R8 = Resistor [tolerance=±5% power=0.25 resistance=10k package=THT]
  C3 = Ceramic Capacitor [capacitance=100nF voltage=35V package="100 mil [THT, multilayer]"]
  D1 = Rectifier Diode [part_number=1N4001 package="300 mil [THT]"]  # not connected

nets:
  N1: J1.pin1, R1.Pin_1, S2.Pin_1, S2.Pin_2, Bauteil2.A2
  5V: J1.pin2, J3.pin1, J4.pin2, S1.Pin_3, S1.Pin_4, S2.Pin_3, S2.Pin_4, U1.output_voltage, LCM1.5V, J8.pin1, C2.+, S3.Pin_4, J7.vcc, Driver1.Vmotor
  N2: J2.pin2, Bauteil2.VIN
  N3: J3.pin2, S1.Pin_1, S1.Pin_2, Bauteil2.A1, R2.Pin_1
  N4: J4.pin1, Bauteil2.A3, S3.Pin_1, S3.Pin_2, R3.Pin_1
  N5: J5.pin1, J6.pin2, R5.Pin_0, R7.Pin_1
  GND: J5.pin2, J6.pin1, R1.Pin_0, U1.GND, Bauteil2.GND, LCM1.GND, C1.-, J8.pin2, C2.-, R2.Pin_0, R3.Pin_0, J7.gnd, R4.Pin_0, R6.Pin_0, Driver1.GND, Q2.source, R8.Pin_1, C3.1
  N6: U1.input_voltage, C1.+
  N7: Bauteil2.A0, R7.Pin_0, R8.Pin_0, C3.0
  N8: Bauteil2.SDA, LCM1.SDA
  N9: Bauteil2.SCL, LCM1.SCL
  N10: Bauteil2.D2, Driver1.IN1
  N11: Bauteil2.D3, Driver1.IN2
  N12: Bauteil2.D4, Driver1.IN3
  N13: Bauteil2.D5, Driver1.IN4
  N14: Bauteil2.D7, J7.pulse
  N15: Bauteil2.D8, LED1.anode, R4.Pin_1, Q2.gate
  N16: LED1.cathode, R6.Pin_1
  N17: R5.Pin_1, Q2.drain
  N18: SM1.blue-pin, Driver1.blue-pin
  N19: SM1.pink-pin, Driver1.pink-pin
  N20: SM1.yellow-pin, Driver1.yellow-pin
  N21: SM1.orange-pin, Driver1.orange-pin
  N22: SM1.red-pin, Driver1.red-pin

notes:
  Netzteil 9V 0,3 A
  0,33 µF
  0,1 µF
  L7805CV
  Endkontakt Batterie
  LCD LCM1602
  Batterie
  Messstelle
  Voltmeter
  28BYJ-48
  IRF520
  Taster Start
  und Automatik
  Taster Stepper
  ULN2003
  AZ-Delivery DatenLogger
  Arduino-Uno im Hintergrund
  Revolver
  Falle (Trap)
  Schutzschaltung

custom parts:
  Adafruit Datalogger Shield v1: Here's a handy Arduino shield: we've had a lot of people looking for a dedicated and well-designed data logging shield. We worked hard to engineer an inexpensive but well-rounded design. Not only is it easy to assemble and customize, it also comes with great documentation and libraries. New! we now are carrying an 'assembled' version of this shield, with all the components pre-soldered. NOTE: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
  LCM1602: Encoder für LCD-Display
  28BYJ-48 Stepper Motor: Unipolar Stepper Motor 28BYJ-48 Top coil - pink & orange Bottom coil - blue & yellow Common rail - red Connector pins: blue - pink - yellow - orange - red
  28BYJ-48 Driver Module: ULN2003 Driver Module for the 28BYJ-48 Unipolar Stepper Motor LED A - Blue wire - Bottom coil left LED B - Pink wire - Top coil left LED C - Yellow wire - Bottom coil right LED D - Orange wire - Top coil right Common rail - red Connector pins: blue - pink - yellow - orange - red Control pins - IN1 to IN4 Power pins - GND & Vmotor (5-12V) On/Off jumper (if removed, power to motor is cut).
