# Fritzing sketch ESP32 VL53L0X (saved by Fritzing 1.0.2b)
breadboards: 2

parts:
  HC-SR04_Sensor_1 = HC-SR04 Ultrasonic Distance Sensor
  Bauteil1 = Adafruit VL530X Time of Flight Distance Sensor [part_number="Adafruit #3317"]
  OLED_I2C1 = OLED 128x64 I2C Monochrome Display
  U1 = ESP32S-HiLetgo [part_number=ESP32S-HiLetgo]
  Bauteil2 = FTDI Basic Programmer
  S3 = Momentary Switch [package=ksa_sealed_tac_switch]

nets:
  GND: HC-SR04_Sensor_1.GND, OLED_I2C1.GND
  VCC: Bauteil1.VCC, OLED_I2C1.VDD, Bauteil2.POWER, S3.1
  GND_2: Bauteil1.GND, Bauteil2.GND
  N1: Bauteil1.SCL, OLED_I2C1.SCK
  N2: Bauteil1.SDA, OLED_I2C1.SDA
  N3: U1.GPIO32, S3.4
  N4: U1.GPIO16, Bauteil2.RXI
  N5: U1.GPIO17, Bauteil2.TXO

notes:
  USB-UART
  HC-SR04
  VL53L0X
  OLED
  ESP32

custom parts:
  Adafruit VL530X Time of Flight Distance Sensor: The VL53L0X is a Time of Flight distance sensor like no other you've used! The sensor contains a very tiny invisible laser source, and a matching sensor. The VL53L0X can detect the "time of flight", or how long the light has taken to bounce back to the sensor. Since it uses a very narrow light source, it is good for determining distance of only the surface directly in front of it. Unlike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
  ESP32S-HiLetgo: HiLetgo ESP-WROOM-32 ESP32 ESP-32S Development Board 2.4GHz Dual-Mode WiFi + Bluetooth Dual Cores Microcontroller The ESP32 integrated with Antenna switches, RF Balun, power amplifiers, low-noise amplifiers, filters, and management modules, and the entire solution occupies the least area of PCB. 2.4 GHz Wi-Fi plus Bluetooth dual-mode chip, with TSMC Ultra-low power consumption 40nm technology,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
