# Fritzing sketch NeoPixel (saved by Fritzing 1.0.2b)
breadboards: 1

parts:
  J2 = Screw terminal - 2 pins [package=THT]
  LCD1 = LCD screen  # not connected
  LCM1 = LCM1602
  J3 = screw terminal, 3 pins
  NEOPIXEL1 = Neopixel Strip -- Black (30/m)
  A1 = Arduino UNO R4 WiFi
  RE1 = KY-040 Rotary encoder [package=THT]

nets:
  GND: J2.pin1, LCM1.GND, A1.Pin_18, A1.Pin_48, RE1.GND
  5V: J2.pin2, LCM1.5V, A1.Pin_11, RE1.Vcc
  N1: LCM1.SDA, A1.Pin_50
  N2: LCM1.SCL, A1.Pin_51
  N3: J3.pin1, NEOPIXEL1.GND
  N4: J3.pin2, NEOPIXEL1.DI
  N5: J3.pin3, NEOPIXEL1.+5V
  N6: A1.Pin_36, RE1.DT
  N7: A1.Pin_37, RE1.CLK

notes:
  geregeltes Netzteil 5 V
  NeoPixel-Led-Streifen
  Farbwert einstellen
  LCM1602

custom parts:
  LCM1602: Encoder für LCD-Display
  Neopixel Strip -- Black (30/m): Neopixel Strip, Black, 30 pixels per meter.
  Arduino UNO R4 WiFi: The Arduino UNO R4 WiFi merges the RA4M1 microprocessor from Renesas with the ESP32-S3 from Espressif, creating an all-in-one tool for makers with enhanced processing power and a diverse array of new peripherals.
  KY-040 Rotary encoder: KY-040 Rotary Encoder with switch on breakout borad from AZ Delivery
