# Fritzing sketch RGB manual (saved by Fritzing 1.0.2b)
breadboards: 1

parts:
  R1 = 6mm Trimmer Potentiometer [maximum_resistance=50kΩ knob_status=50% power=0.5W package=THT]
  R2 = Resistor [tolerance=±5% resistance=220 package="0402 [SMD]"]
  R3 = Resistor [tolerance=±5% resistance=220 package="0402 [SMD]"]
  R4 = Resistor [tolerance=±5% resistance=220 package="0402 [SMD]"]
  LED1 = RGB LED (com. cathode, rbg) [color="Red (633nm)" current=0.030A package="5 mm [THT]"]
  R5 = 6mm Trimmer Potentiometer [maximum_resistance=1kΩ knob_status=50% power=0.5W package=THT]  # not connected
  R6 = 6mm Trimmer Potentiometer [maximum_resistance=1kΩ knob_status=50% power=0.5W package=THT]  # not connected
  R7 = 6mm Trimmer Potentiometer [maximum_resistance=1kΩ knob_status=50% power=0.5W package=THT]  # not connected
  J1 = screw terminal, 2 pins

nets:
  N1: R1.wiper, LED1.common_cathode
  N2: R1.leg2, J1.pin1
  N3: R2.Pin_0, LED1.green_anode
  N4: R3.Pin_0, LED1.blue_anode
  N5: R4.Pin_0, LED1.red_anode

notes:
  RGB-LED
  geregeltes Netzteil 5 V
  Trimmer 1 kOhm
  rot      grün     blau                 Lichtstärke
  Trimmer 5  kOhm
  Widerstand 220 Ohm
