# Fritzing sketch RGB trimmer Arduino (saved by Fritzing 1.0.2b)
breadboards: 2

parts:
  J2 = Screw terminal - 2 pins [package=THT]
  Bauteil1 = Arduino Uno (Rev3)
  LCD1 = LCD screen  # not connected
  LCM1 = LCM1602
  IC1 = SELECTOR_MULTIPLEXER [package=dil16]
  LED1 = RGB LED (com. cathode, rgb) [color="Red (633nm)" current=0.030A package="5 mm [THT]"]
  R1 = Trimmer Potentiometer [maximum_resistance=10kΩ knob_status=50% power=0.5W package=THT]
  R2 = Trimmer Potentiometer [maximum_resistance=10kΩ knob_status=50% power=0.5W package=THT]
  R3 = Trimmer Potentiometer [maximum_resistance=10kΩ knob_status=50% power=0.5W package=THT]
  R4 = Trimmer Potentiometer [maximum_resistance=10kΩ knob_status=50% power=0.5W package=THT]  # not connected
  R5 = Trimmer Potentiometer [maximum_resistance=10kΩ knob_status=50% power=0.5W package=THT]  # not connected
  R6 = Trimmer Potentiometer [maximum_resistance=10kΩ knob_status=50% power=0.5W package=THT]  # not connected
  R7 = Trimmer Potentiometer [maximum_resistance=10kΩ knob_status=50% power=0.5W package=THT]  # not connected
  R8 = Resistor [tolerance=±5% resistance=220 package="2010 [SMD]"]
  R9 = Resistor [tolerance=±5% resistance=220 package="2010 [SMD]"]
  R10 = Resistor [tolerance=±5% resistance=220 package="2010 [SMD]"]

nets:
  GND: J2.pin1, Bauteil1.GND, LCM1.GND, IC1.A_2B, IC1.A_2Y, IC1.P_GND, IC1.A_4Y, R1.leg1, R2.leg1, R2.leg2, R3.leg1
  VIN: J2.pin2, Bauteil1.VIN, LCM1.5V, IC1.P_VCC, R1.leg2, R3.leg2
  N1: Bauteil1.A0, IC1.A_1B
  N2: Bauteil1.D9_PWM, R8.Pin_1
  N3: Bauteil1.D10_PWM/SS, R9.Pin_1
  N4: Bauteil1.D11_PWM/MOSI, R10.Pin_1
  N5: Bauteil1.A4/SDA, LCM1.SDA
  N6: Bauteil1.A5/SCL, LCM1.SCL
  N7: Bauteil1.D2, IC1.A_3A
  N8: Bauteil1.D3_PWM, IC1.A_3B
  N9: Bauteil1.D4, IC1.A_3Y
  N10: IC1.A_4B, R1.wiper
  N11: IC1.A_4A, R2.wiper
  N12: IC1.A_G, R3.wiper
  N13: LED1.red_anode, R8.Pin_0
  N14: LED1.green_anode, R9.Pin_0
  N15: LED1.blue_anode, R10.Pin_0

notes:
  geregeltes Netzteil 5 V
  RGB-LED
  rot           grün          blau                                                    rot             grün            blau        Lichtstärke
  kalibrieren
  Farbe einstellen
  Multiplexer MC14051B
  Trimmer 10 kΩ
  LCM1602

custom parts:
  LCM1602: Encoder für LCD-Display
