# Fritzing sketch ESP32 tinybasic (saved by Fritzing 1.0.2b)
breadboards: 2

parts:
  U1 = ESP32S-HiLetgo [part_number=ESP32S-HiLetgo]
  S3 = Momentary Switch [package=ksa_sealed_tac_switch]
  R1 = 12mm Trimmer Potentiometer (Large) [maximum_resistance=10kΩ knob_status=50% power=0.5W package=THT]
  R2 = Resistor [tolerance=±5% power=0.25W resistance=330 package=THT]
  R3 = Resistor [tolerance=±5% power=0.25W resistance=10k package=THT]
  LCM1 = LCM1602
  LCD1 = LCD screen  # not connected
  J1 = Piezo Speaker
  LED1 = LED - 5mm [color="Yellow (595nm)" current=0.030A package="5 mm [THT]"]
  LED2 = LED - 5mm [color="Red (633nm)" current=0.030A package="5 mm [THT]"]
  LED3 = LED - 5mm [color="Green (565nm)" current=0.030A package="5 mm [THT]"]
  LED4 = LED - 5mm [color="Yellow (595nm)" current=0.030A package="5 mm [THT]"]
  R4 = Resistor [tolerance=±5% power=0.25W resistance=330 package=THT]
  R5 = Resistor [tolerance=±5% power=0.25W resistance=330 package=THT]
  R6 = Resistor [tolerance=±5% power=0.25W resistance=330 package=THT]
  LED5 = LED - 5mm [color="Red (633nm)" current=0.030A package="5 mm [THT]"]  # not connected
  LED6 = LED - 5mm [color="Yellow (595nm)" current=0.030A package="5 mm [THT]"]  # not connected
  LED7 = LED - 5mm [color="Green (565nm)" current=0.030A package="5 mm [THT]"]  # not connected

nets:
  N1: U1.GPIO2, J1.pin2
  N2: U1.GPIO4, LED3.anode
  N3: U1.GPIO16, LED1.anode
  N4: U1.GPIO17, LED2.anode
  GND: U1.GND, S3.3, R1.leg1, LCM1.GND, J1.pin1, LED4.cathode, R4.Pin_1, R5.Pin_1, R6.Pin_1
  N5: U1.GPIO21, LCM1.SDA
  N6: U1.GPIO22, LCM1.SCL
  N7: S3.1, R3.Pin_1
  N8: R2.Pin_0, LED4.anode

notes:
  Potentiometer
  Piezo Speaker
  LCM1602 I2C
  5 V
  ESP32
  3 V
  GPIO 17
  GPIO 16
  GPIO 4
  GPIO 35
  GPIO 14
  GPIO 2
  GPIO 22 SCL
  GPIO 21 SDA
  GPIO 32
  GPIO 33
  GPIO 25
  Ampelgruppe H
  Ampelgruppe N
  GPIO 13

custom parts:
  ESP32S-HiLetgo: HiLetgo ESP-WROOM-32 ESP32 ESP-32S Development Board 2.4GHz Dual-Mode WiFi + Bluetooth Dual Cores Microcontroller The ESP32 integrated with Antenna switches, RF Balun, power amplifiers, low-noise amplifiers, filters, and management modules, and the entire solution occupies the least area of PCB. 2.4 GHz Wi-Fi plus Bluetooth dual-mode chip, with TSMC Ultra-low power consumption 40nm technology,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
  LCM1602: Encoder für LCD-Display
